# Fritzing sketch Schema00 (saved by Fritzing 0.9.3b)
breadboards: 1

parts:
  LED1 = LED - 5mm [color="Red (633nm)" package="5 mm [THT]"]
  Teensy_3_1 = Teensy 3.1  # not connected
  R1 = Resistor [tolerance=±5% resistance=220 package=THT]

nets:
  N1: LED1.anode, R1.Pin_1
