# Fritzing sketch Schema01 (saved by Fritzing 0.9.3b)
breadboards: 1

parts:
  R1 = Resistor [tolerance=±5% resistance=220 package=THT]
  LED1 = LED - 5mm [color="Red (633nm)" package="5 mm [THT]"]
  Teensy_3_1 = Teensy 3.1  # not connected

nets:
  N1: R1.Pin_1, LED1.anode
