# Fritzing sketch Schema02 (saved by Fritzing 0.9.3b)
breadboards: 1

parts:
  LED1 = LED - 5mm [color="Red (633nm)" package="5 mm [THT]"]
  Teensy_3_1 = Teensy 3.1  # not connected
  R1 = Resistor [tolerance=±5% resistance=220 package=THT]
  S1 = Pushbutton [package="[THT]"]
  R2 = Resistor [tolerance=±5% resistance=10k package="2512 [SMD]"]

nets:
  N1: LED1.cathode, R2.Pin_1
  N2: LED1.anode, R1.Pin_1
  N3: S1.Pin_1, S1.Pin_2, R2.Pin_0
  N4: S1.Pin_3, S1.Pin_4
